# Fritzing sketch ArduinoPBD (saved by Fritzing 0.9.2b)
breadboards: 1

parts:
  Part1 = Arduino Uno (Rev3)
  S1 = Pushbutton [package="[THT]"]
  R1 = Photocell (LDR) [package=THT]
  T1 = LM35 Temperature Sensor [package="TO92 [THT]"]
  LED1 = LED - 5mm [color="Red (633nm)" package="5 mm [THT]"]
  7_Segment1 = 7 Segment Display
  7_Segment2 = 7 Segment Display
  IC1 = IC, DIP package, 14 pins [chip_label=74164]
  SPKR1 = Loudspeaker
  M1 = DC Motor
  R2 = Resistor [tolerance=±5% resistance=10k package=THT]
  R3 = Resistor [tolerance=±5% resistance=1k package=THT]
  R5 = Resistor [tolerance=±5% resistance=100 package=THT]
  R6 = Resistor [tolerance=±5% resistance=100 package=THT]
  C2 = Ceramic Capacitor [capacitance=1µF package="200 mil [THT, multilayer]"]
  C3 = Ceramic Capacitor [capacitance=1µF package="200 mil [THT, multilayer]"]
  LED2 = LED - 5mm [color="Red (633nm)" package="5 mm [THT]"]
  R8 = Resistor [tolerance=±5% resistance=1k package=THT]
  R9 = Resistor [tolerance=±5% resistance=10k package=THT]
  IC2 = IC, DIP package, 14 pins [chip_label=74164]

nets:
  N1: Part1.A0, T1.Vout
  N2: Part1.A1, R1.pin_1, R2.Pin_0
  N3: Part1.AREF, Part1.3V3, R1.pin_0, T1.+Vs, R8.Pin_0
  N4: Part1.D0/RX, IC1.pin1, IC1.pin2
  N5: Part1.D1/TX, IC2.pin1, IC2.pin2
  N6: Part1.D2, IC1.pin8, IC2.pin8
  N7: Part1.D3_PWM, R6.Pin_0
  N8: Part1.D4, IC1.pin9, IC2.pin9
  N9: Part1.D5_PWM, R5.Pin_0
  N10: Part1.D6_PWM, R3.Pin_0
  N11: Part1.D7, S1.Pin_1, S1.Pin_2
  N12: Part1.ioref, Part1.5V, S1.Pin_3, S1.Pin_4
  GND: Part1.GND, T1.GND, LED1.cathode, 7_Segment1.common_anode, 7_Segment2.common_anode, IC1.pin7, SPKR1.pin1, M1.pin_1, R2.Pin_1, C2.1, LED2.cathode, R9.Pin_0, IC2.pin7
  N13: LED1.anode, R3.Pin_1, LED2.anode
  N14: 7_Segment1.Segment_E, IC1.pin3
  N15: 7_Segment1.Segment_D, IC1.pin4
  N16: 7_Segment1.Segment_C, IC1.pin5
  N17: 7_Segment1.Segment_DP, IC1.pin6
  N18: 7_Segment1.Segment_B, IC1.pin10
  N19: 7_Segment1.Segment_A, IC1.pin11
  N20: 7_Segment1.Segment_F, IC1.pin12
  N21: 7_Segment1.Segment_G, IC1.pin13
  N22: 7_Segment2.Segment_E, IC2.pin3
  N23: 7_Segment2.Segment_D, IC2.pin4
  N24: 7_Segment2.Segment_C, IC2.pin5
  N25: 7_Segment2.Segment_DP, IC2.pin6
  N26: 7_Segment2.Segment_B, IC2.pin10
  N27: 7_Segment2.Segment_A, IC2.pin11
  N28: 7_Segment2.Segment_F, IC2.pin12
  N29: 7_Segment2.Segment_G, IC2.pin13
  N30: IC1.pin14, R8.Pin_1, R9.Pin_1, IC2.pin14
  N31: SPKR1.pin2, R6.Pin_1, C2.0
  N32: M1.pin_2, R5.Pin_1, C3.0

notes:
  TODO:
  - check ioref
  DIGITAL PINS
  0 [o] 7seg 10s
  1 [o] 7seg 1s
  2 [o] 164 Clock Pulse
  3 [o~] Speaker
  4 [o] 164 Reset
  5 [o~] motor
  6 [o] LED
  7 [I] test switch
  ANALOG INPUT PINS
  0 Temp Sensor
  1 Light Sensor
  2
  3
  4
  5
  WIRE COLOR CODE
  Black Ground
  Red 5V
  Orange 3.3V
  Blue Digital 0-5V
  Pink PWM 0-5V
  Yellow Analog 0-3.3V
  Green Clock
  Grey Misc
  PBD Arduino Project
