# Fritzing sketch ArduinoPBD2 (saved by Fritzing 0.9.2b)
breadboards: 1

parts:
  Arduino = Arduino Uno (Rev3)
  S1 = Pushbutton [package="[THT]"]
  T1 = LM35 Temperature Sensor [package="TO92 [THT]"]
  LED1 = LED - 5mm [color="Red (633nm)" package="5 mm [THT]"]
  7_Segment_A = 7 Segment Display
  7_Segment_B = 7 Segment Display
  SPKR1 = Loudspeaker
  Motor = DC Motor
  R2 = Resistor [tolerance=±5% resistance=10k package=THT]
  R3 = Resistor [tolerance=±5% resistance=100 package=THT]
  LED2 = LED - 5mm [color="Red (633nm)" package="5 mm [THT]"]
  R5 = Resistor [tolerance=±5% resistance=270 package=THT]
  D1 = Rectifier Diode [part_number=1N4001 package="300 mil [THT]"]
  Q1 = NPN-Transistor [package="TO92 [THT]"]
  C1 = Electrolytic Capacitor [capacitance=1µF voltage=50V package="100 mil [THT, electrolytic]"]
  R4 = Resistor [tolerance=±5% resistance=100 package=THT]
  C2 = Electrolytic Capacitor [capacitance=1µF voltage=50V package="100 mil [THT, electrolytic]"]
  SR1 = IC, DIP package, 14 pins [chip_label=74164]
  SR2 = IC, DIP package, 14 pins [chip_label=74164]
  R1 = Photocell (LDR) [package=THT]
  R6 = Resistor [tolerance=±5% resistance=10k package=THT]
  R7 = Resistor [tolerance=±5% resistance=270 package=THT]

nets:
  Temp: Arduino.A0, T1.Vout, R6.Pin_1
  LDR: Arduino.A1, R2.Pin_0, R1.pin_1
  7seg A: Arduino.D8, SR1.pin1, SR1.pin2
  7seg B: Arduino.D9_PWM, SR2.pin1, SR2.pin2
  3.3V: Arduino.AREF, Arduino.3V3, SR1.pin14, SR2.pin14, R1.pin_0
  N1: Arduino.D2, S1.Pin_1, S1.Pin_2, R7.Pin_1
  N2: Arduino.D3_PWM, SPKR1.pin2
  reset: Arduino.D4, SR1.pin9, SR2.pin9
  motor: Arduino.D5_PWM, R5.Pin_0
  LED: Arduino.D6_PWM, R3.Pin_0, R4.Pin_0
  clock: Arduino.D7, SR1.pin8, SR2.pin8
  5V: Arduino.5V, S1.Pin_3, S1.Pin_4, T1.+Vs, Motor.pin_2, D1.cathode
  GND: Arduino.GND, T1.GND, LED1.cathode, 7_Segment_A.common_anode, 7_Segment_B.common_anode, SPKR1.pin1, R2.Pin_1, LED2.cathode, Q1.E, C1.-, C2.-, SR1.pin7, SR2.pin7, R6.Pin_0, R7.Pin_0
  N3: LED1.anode, R3.Pin_1, C1.+
  N4: 7_Segment_A.Segment_E, SR1.pin3
  N5: 7_Segment_A.Segment_D, SR1.pin4
  N6: 7_Segment_A.Segment_C, SR1.pin5
  N7: 7_Segment_A.Segment_DP, SR1.pin6
  N8: 7_Segment_A.Segment_B, SR1.pin10
  N9: 7_Segment_A.Segment_A, SR1.pin11
  N10: 7_Segment_A.Segment_F, SR1.pin12
  N11: 7_Segment_A.Segment_G, SR1.pin13
  N12: 7_Segment_B.Segment_E, SR2.pin3
  N13: 7_Segment_B.Segment_D, SR2.pin4
  N14: 7_Segment_B.Segment_C, SR2.pin5
  N15: 7_Segment_B.Segment_DP, SR2.pin6
  N16: 7_Segment_B.Segment_B, SR2.pin10
  N17: 7_Segment_B.Segment_A, SR2.pin11
  N18: 7_Segment_B.Segment_F, SR2.pin12
  N19: 7_Segment_B.Segment_G, SR2.pin13
  N20: Motor.pin_1, D1.anode, Q1.C
  N21: LED2.anode, R4.Pin_1, C2.+
  N22: R5.Pin_1, Q1.B

notes:
  DIGITAL PINS
  2 [i] Switch (interrupt)
  3 [o~] Speaker
  4 [o] 164 Reset
  5 [o~] motor
  6 [o~] LED
  7 [o] 164 Clock Pulse
  8 [o] 7seg 10s
  9 [o] 7seg 1s
  ANALOG INPUT PINS
  0 Temp Sensor
  1 Light Sensor
  2
  3
  4
  5
  WIRE COLOR CODE
  Black Ground
  Red 5V
  Orange 3.3V
  Blue Digital 0-5V
  Pink PWM 0-5V
  Yellow Analog 0-3.3V
  Green Clock
  Grey Misc
  PBD Arduino Project
  makeshift:
  AREF
  A0
  A1
  D6
  Platform Based Development, Temperature display with overheat alarm, fire alarm and active cooling fan, 2
